// Logisim project circuit.circ as structural Verilog: 1 circuit, main circuit main
module main (
  input  CLC,
  input  x0,
  input  x1,
  input  x2,
  output Y0,
  output Y1,
  output Y2
);

  wire and_1_out, and_2_out, and_3_out, and_5_out, and_6_out, and_7_out, d_ff_1_q, d_ff_2_q, not_1_out,
       not_2_out, not_3_out, not_4_out, not_5_out, or_1_out, or_2_out, or_4_out, or_5_out;

  not not_1 (not_1_out, x0);
  not not_2 (not_2_out, d_ff_2_q);
  not not_3 (not_3_out, d_ff_1_q);
  and and_1 (and_1_out, d_ff_1_q, x0);
  not not_4 (not_4_out, x1);
  not not_5 (not_5_out, x2);
  or or_1 (or_1_out, d_ff_2_q, and_1_out);
  or or_2 (or_2_out, d_ff_1_q, d_ff_2_q);
  and and_2 (and_2_out, d_ff_1_q, d_ff_2_q, x2);
  and and_3 (and_3_out, x2, not_2_out, not_3_out);
  and and_4 (Y1, not_3_out, x2);
  not not_6 (Y2, x2);
  and and_5 (and_5_out, d_ff_1_q, not_4_out, not_5_out);
  and and_6 (and_6_out, not_5_out, not_4_out, or_1_out);
  and and_7 (and_7_out, not_1_out, x1, or_2_out);
  or or_3 (Y0, and_2_out, and_3_out);
  or or_4 (or_4_out, and_5_out, x2);
  or or_5 (or_5_out, and_6_out, and_7_out);
  D_Flip_Flop d_ff_1 (.clk(CLC), .D(or_4_out), .Q(d_ff_1_q));  // open: Qn, preset, en, reset
  D_Flip_Flop d_ff_2 (.clk(CLC), .D(or_5_out), .Q(d_ff_2_q));  // open: Qn, preset, en, reset

  // Notes on the sheet:
  //   x2
  //   x1
  //   x0
  //   Q1
  //   Q0
endmodule
